// Logisim project M-1.circ as structural Verilog: 7 circuits, main circuit main
module main (
  input  in_1,
  input  [7:0] in_2,
  output [7:0] out_3,
  output [7:0] out_4
);

  wire binairy_to_bcd_converter_1_p1, binairy_to_bcd_converter_1_p3, binairy_to_bcd_converter_1_p5,
       clock_1_out, cpu_1_out_8, d_ff_1_q;
  wire [3:0] cpu_1_out_17;
  wire [7:0] cpu_1_a, cpu_1_b, cpu_1_c, cpu_1_d, cpu_1_ins, cpu_1_operand, cpu_1_out_6, cpu_1_out_16,
       multiplexer_1_out, ram_1_dout;
  wire [11:0] cpu_1_adrr_out, cpu_1_pc;

  Clock clock_1 (.out(clock_1_out));
  D_Flip_Flop d_ff_1 (.clk(clock_1_out), .D(in_1), .Q(d_ff_1_q));  // open: Qn, preset, reset
  RAM #(.addrWidth(12)) ram_1 (
    .addr(cpu_1_adrr_out), .we(cpu_1_out_8), .clk(clock_1_out), .din(multiplexer_1_out), .dout(ram_1_dout));
  Multiplexer #(.enable("false"), .width(8)) multiplexer_1 (
    .in0(cpu_1_out_6), .in1(in_2), .out(multiplexer_1_out), .sel(d_ff_1_q));
  CPU cpu_1 (
    .in_1(ram_1_dout), .CLK(clock_1_out), .CLR(d_ff_1_q), .out_4(out_3), .out_5(out_4), .out_6(cpu_1_out_6),
    .Adrr_Out(cpu_1_adrr_out), .out_8(cpu_1_out_8), .A(cpu_1_a), .B(cpu_1_b), .C(cpu_1_c), .D(cpu_1_d),
    .PC(cpu_1_pc), .Operand(cpu_1_operand), .INS(cpu_1_ins), .out_16(cpu_1_out_16), .out_17(cpu_1_out_17));
  // Probe on cpu_1_a
  // Probe on cpu_1_b
  // Probe on cpu_1_c
  // Probe on cpu_1_d
  // Probe on cpu_1_pc
  // Probe on cpu_1_operand
  // Probe on cpu_1_ins
  // Probe on cpu_1_out_17
  Hex_Digit_Display hex_digit_display_1 ();  // open: value, dp
  Hex_Digit_Display hex_digit_display_2 ();  // open: value, dp
  // Binairy_to_BCD_converter #(.binvalue(8)) binairy_to_bcd_converter_1: pin names not known; wires that end beside it: binairy_to_bcd_converter_1_p1, binairy_to_bcd_converter_1_p1, binairy_to_bcd_converter_1_p3, binairy_to_bcd_converter_1_p3, binairy_to_bcd_converter_1_p5, cpu_1_out_16, binairy_to_bcd_converter_1_p5
  Hex_Digit_Display hex_digit_display_3 ();  // open: value, dp
endmodule

module CPU (
  input  [7:0] in_1,
  input  CLK,
  input  CLR,
  output [7:0] out_4,
  output [7:0] out_5,
  output [7:0] out_6,
  output [11:0] Adrr_Out,
  output out_8,
  output [7:0] A,
  output [7:0] B,
  output [7:0] C,
  output [7:0] D,
  output [11:0] PC,
  output [7:0] Operand,
  output [7:0] INS,
  output [7:0] out_16,
  output [3:0] out_17
);

  wire control_unit_1_clear_flags, control_unit_1_dest_in, control_unit_1_flags_in, control_unit_1_if_carry,
       control_unit_1_if_zero, control_unit_1_ins_in, control_unit_1_j, control_unit_1_math_with_operand,
       control_unit_1_opr_in, control_unit_1_output_in, control_unit_1_pc_2, control_unit_1_pc_in,
       control_unit_1_set_a_to_src;
  wire [1:0] control_unit_1_ab_select, multiplexer_2_out;
  wire [2:0] control_unit_1_db_select;
  wire [7:0] alu_and_flags_1_output, multiplexer_1_out, multiplexer_3_out;
  wire [11:0] pc_control_1_pc_out;

  Register u_INS (.D(out_6), .Q(INS), .clk(control_unit_1_ins_in), .clr(CLR));  // open: en
  Register OPR (.D(out_6), .Q(Operand), .clk(control_unit_1_opr_in), .clr(CLR));  // open: en
  Control_Unit control_unit_1 (
    .INS(out_6), .CLK(CLK), .CLR(CLR), .AB_Select(control_unit_1_ab_select),
    .DB_select(control_unit_1_db_select), .Set_A_to_src(control_unit_1_set_a_to_src), .RAM_in(out_8),
    .Dest_In(control_unit_1_dest_in), .PC_In(control_unit_1_pc_in), .Flags_In(control_unit_1_flags_in),
    .INS_in(control_unit_1_ins_in), .OPR_in(control_unit_1_opr_in), .PC_2(control_unit_1_pc_2),
    .J(control_unit_1_j), .If_Zero(control_unit_1_if_zero), .If_Carry(control_unit_1_if_carry),
    .Math_with_Operand(control_unit_1_math_with_operand), .Clear_Flags(control_unit_1_clear_flags),
    .Output_In(control_unit_1_output_in));
  Multiplexer #(.enable("false"), .width(8)) multiplexer_1 (
    .in0(out_4), .in1(out_5), .out(multiplexer_1_out), .sel(control_unit_1_math_with_operand));
  // Probe on out_4
  Multiplexer #(.enable("false"), .width(2)) multiplexer_2 (
    .in0(Operand[1:0]), .in1(INS[3:2]), .out(multiplexer_2_out), .sel(control_unit_1_math_with_operand));
  Multiplexer #(.enable("false"), .width(8)) multiplexer_3 (
    .in0(out_5), .in1(Operand), .out(multiplexer_3_out), .sel(control_unit_1_math_with_operand));
  Registers registers_1 (
    .INS(INS[3:0]), .Write_Dest(control_unit_1_dest_in), .Data_In(out_6), .CLR(CLR),
    .Set_A_to_dest(control_unit_1_set_a_to_src), .Source(out_4), .Dest(out_5), .A(A), .B(B), .C(C), .D(D));
  // Probe on out_5
  ALU_and_Flags alu_and_flags_1 (
    .X(multiplexer_1_out), .Y(multiplexer_3_out), .ALU_Control(multiplexer_2_out),
    .Flags_In(control_unit_1_flags_in), .Clear_Flags(control_unit_1_clear_flags), .in_6(CLR),
    .Output(alu_and_flags_1_output), .out_9(out_17));  // open: in_7
  Multiplexer #(.enable("false"), .select(3), .width(8)) multiplexer_4 (
    .in0(in_1), .in1(INS), .in2(Operand), .in3(out_4), .in4(out_5), .in5(alu_and_flags_1_output), .in6(A),
    .out(out_6), .sel(control_unit_1_db_select));  // open: in7
  Register register_1 (.D(out_6), .Q(out_16), .clk(control_unit_1_output_in), .clr(CLR));  // open: en
  PC_Control pc_control_1 (
    .PC_out(pc_control_1_pc_out), .J(control_unit_1_j), .PC_2(control_unit_1_pc_2),
    .If_Zero(control_unit_1_if_zero), .If_Carry(control_unit_1_if_carry), .Flags(out_17), .PC(PC),
    .OPR({INS[3:0], Operand}));
  Multiplexer #(.enable("false"), .select(2), .width(12)) multiplexer_5 (
    .in0(PC), .in1(pc_control_1_pc_out), .in2({INS[3:0], Operand}), .out(Adrr_Out),
    .sel(control_unit_1_ab_select));  // open: in3
  Register #(.width(12)) u_PC (.D(pc_control_1_pc_out), .Q(PC), .clk(control_unit_1_pc_in), .clr(CLR));  // open: en
endmodule

module PC_Control (
  input  [3:0] Flags,
  input  [11:0] PC,
  input  [11:0] OPR,
  input  J,
  input  PC_2,
  input  If_Zero,
  input  If_Carry,
  output [11:0] PC_out
);

  wire and_1_out, not_1_out, not_2_out, or_1_out, or_2_out;
  wire [11:0] adder_1_out, multiplexer_1_out;

  not not_1 (not_1_out, If_Zero);
  not not_2 (not_2_out, If_Carry);
  Multiplexer #(.enable("false"), .width(12)) multiplexer_1 (
    .in0(12'h1), .in1(12'h2), .out(multiplexer_1_out), .sel(PC_2));
  or or_1 (or_1_out, Flags[1], not_1_out);
  or or_2 (or_2_out, Flags[0], not_2_out);
  and and_1 (and_1_out, J, or_1_out, or_2_out);
  Adder #(.width(12)) adder_1 (.a(PC), .b(multiplexer_1_out), .out(adder_1_out));  // open: cin, cout
  Multiplexer #(.enable("false"), .width(12)) multiplexer_2 (
    .in0(adder_1_out), .in1(OPR), .out(PC_out), .sel(and_1_out));
endmodule

module Control_Unit (
  input  [7:0] INS,
  input  CLK,
  input  CLR,
  output [1:0] AB_Select,
  output [2:0] DB_select,
  output Set_A_to_src,
  output RAM_in,
  output Dest_In,
  output PC_In,
  output Flags_In,
  output INS_in,
  output OPR_in,
  output PC_2,
  output J,
  output If_Zero,
  output If_Carry,
  output Math_with_Operand,
  output Clear_Flags,
  output Output_In
);

  wire and_1_out, or_1_out;
  wire [7:0] adder_1_out, multiplexer_1_out, register_1_q, rom_1_data;
  wire [13:2] rom_2_data;

  ROM rom_1 (.addr(INS), .data(rom_1_data));
  or or_1 (or_1_out, CLR, rom_2_data[2]);
  and and_1 (and_1_out, CLK, ~or_1_out);  // AND_Gate
  Multiplexer #(.enable("false"), .width(8)) multiplexer_1 (
    .in0(adder_1_out), .in1(rom_1_data), .out(multiplexer_1_out), .sel(rom_2_data[12]));
  Register register_1 (.D(multiplexer_1_out), .Q(register_1_q), .clk(and_1_out), .clr(CLR));  // open: en
  Adder adder_1 (.a(register_1_q), .b(8'h1), .out(adder_1_out));  // open: cin, cout
  ROM #(.dataWidth(20)) rom_2 (
    .addr(register_1_q),
    .data({Clear_Flags, Math_with_Operand, If_Carry, If_Zero, J, PC_2, rom_2_data[13:8], Output_In, Set_A_to_src, DB_select, rom_2_data[2], AB_Select}));
  Multiplexer #(.enable("false"), .width(6)) multiplexer_2 (
    .in0(rom_2_data[13:8]), .in1({6{1'b0}}), .out({OPR_in, INS_in, Flags_In, PC_In, Dest_In, RAM_in}),
    .sel(and_1_out));

  // Notes on the sheet:
  //   contents of rom_1 (hex, n*v repeats v):
  //   0 3 0 9 c 10*0 fd 16*10 16*14 16*6 16*18 16*1b 16*20 16*30 16*33 16*36 16*40 16*f8
  //   contents of rom_2 (hex, n*v repeats v):
  //   0 400 1000 0 80000 1000 2001 8400 1000 7*0 2001 4610 1000 2001 0 618 1000 0 2001 84e28 1000 2001
  //   44e28 1000 0 0 2001 4742 1000 13*0 2001 1c400 1000 2001 28400 1000 2001 4532 1000 9*0 1000 181*0 20
  //   4a0 1020 0 0 4 4 4
endmodule

module Registers (
  input  [3:0] INS,
  input  Write_Dest,
  input  [7:0] Data_In,
  input  CLR,
  input  Set_A_to_dest,
  output [7:0] Source,
  output [7:0] Dest,
  output [7:0] A,
  output [7:0] B,
  output [7:0] C,
  output [7:0] D
);

  wire decoder_1_out0, decoder_1_out1, decoder_1_out2, decoder_1_out3;
  wire [1:0] multiplexer_1_out;

  Multiplexer #(.enable("false"), .width(2)) multiplexer_1 (
    .in0(INS[1:0]), .in1(2'b00), .out(multiplexer_1_out), .sel(Set_A_to_dest));
  Decoder #(.enable("false"), .select(2)) decoder_1 (
    .out0(decoder_1_out0), .out1(decoder_1_out1), .out2(decoder_1_out2), .out3(decoder_1_out3),
    .sel(multiplexer_1_out));
  Register u_A (.D(Data_In), .en(decoder_1_out0), .Q(A), .clk(Write_Dest), .clr(CLR));
  Register u_C (.D(Data_In), .en(decoder_1_out2), .Q(C), .clk(Write_Dest), .clr(CLR));
  Register u_B (.D(Data_In), .en(decoder_1_out1), .Q(B), .clk(Write_Dest), .clr(CLR));
  Register u_D (.D(Data_In), .en(decoder_1_out3), .Q(D), .clk(Write_Dest), .clr(CLR));
  Multiplexer #(.enable("false"), .select(2), .width(8)) multiplexer_2 (
    .in0(A), .in1(B), .in2(C), .in3(D), .out(Source), .sel(INS[3:2]));
  Multiplexer #(.enable("false"), .select(2), .width(8)) multiplexer_3 (
    .in0(A), .in1(B), .in2(C), .in3(D), .out(Dest), .sel(multiplexer_1_out));
endmodule

// Output
module ALU_and_Flags (
  input  [7:0] X,
  input  [7:0] Y,
  input  [1:0] ALU_Control,
  input  Flags_In,
  input  Clear_Flags,
  input  in_6,
  input  in_7,
  output [7:0] Output,
  output [3:0] out_9
);

  wire [3:0] adder_1_cout, multiplexer_3_out;
  wire [7:0] adder_1_out, multiplexer_1_out, or_1_out, subtractor_1_out, xor_1_out;

  Multiplexer #(.enable("false"), .width(8)) multiplexer_1 (.in0(Y), .in1(8'h1), .out(multiplexer_1_out), .sel(in_7));
  Adder adder_1 (.a(X), .b(multiplexer_1_out), .out(adder_1_out), .cin(out_9[0]), .cout(adder_1_cout[0]));
  Subtractor subtractor_1 (
    .a(X), .b(multiplexer_1_out), .out(subtractor_1_out), .bin(out_9[2]), .bout(adder_1_cout[2]));
  assign xor_1_out = X ^ multiplexer_1_out;  // XOR_Gate xor_1, 8 bits wide
  assign or_1_out = X | multiplexer_1_out;  // OR_Gate or_1, 8 bits wide
  Multiplexer #(.enable("false"), .select(2), .width(8)) multiplexer_2 (
    .in0(adder_1_out), .in1(subtractor_1_out), .in2(xor_1_out), .in3(or_1_out), .out(Output),
    .sel(ALU_Control));
  Comparator comparator_1 (.a(Output), .b({8{1'b0}}), .eq(adder_1_cout[1]), .lt(adder_1_cout[3]));  // open: gt
  Multiplexer #(.enable("false"), .width(4)) multiplexer_3 (
    .in0(adder_1_cout), .in1(4'b0000), .out(multiplexer_3_out), .sel(Clear_Flags));
  Register #(.width(4)) register_1 (.D(multiplexer_3_out), .Q(out_9), .clk(Flags_In), .clr(in_6));  // open: en
endmodule

module Guide (
);


  // Notes on the sheet:
  //   The M-1 is an 8-bit CPU. It has 18 different instructions and can address 4 kilobytes of RAM. Below are the instructions
  //   and how to use them. Other information is below.
  //   0x00; NOP, No Operation
  //   0x01; CF, clears the flags register
  //   0x1x;LDI, loads the destination register with operand
  //   0x2x; MOV, loads the destination register with the contents of the source register
  //   0x3x; JMP, jumps the PC to the extended operand
  //   0x4x; MWR, Performs ALU operation on source and destination, stores in destination
  //   0x5x; MWO, performs ALU operation on operand and destination, stores in destination
  //   0x6x; LAM. Load the A register with memory address of extended operand
  //   0x7; JZ. Jump the PC to extended operand if zero flag is set
  //   0x8x; JC. Jump the PC to extended operand if the carry flag is set
  //   0x9x; STA. Store the contents of the A register into RAM address specified by extended operand
  //   0x0f; HCF; Halts the processor until clear
  //   0xax; MW1: Performs ALU operation with constant 1 and destination, stores in destination
  //   0xbx; OUT; loads source register to output port
  //   LDI, JMP, MWR, MWO, LAM, JZ, JC, STA, and MW1 Operations require an operand.
  //   With MWO and MW1 operations, only 4 operations are possible(Add, Subtract, OR, and XOR), however with MWR
  //   single-input operations like NOT and shifts are possible using the lowest 3 bits of the operand as the ALU opcode.
endmodule
